// Logisim project Ejercicio1.circ as structural Verilog: 3 circuits, main circuit Half-Adder
module Half_Adder (
  input  x,
  input  y,
  output x_y__xy__prime,
  output Acarreo
);

  wire not_1_out, or_1_out;

  or or_1 (or_1_out, x, y);
  and and_1 (Acarreo, x, y);
  not not_1 (not_1_out, Acarreo);
  and and_2 (x_y__xy__prime, or_1_out, not_1_out);

  // Notes on the sheet:
  //   c = xy
  //   s = xy' + x'y
  //   s = (x+y)(xy)'
  //   x+y
  //   xy
  //   HALF-ADDER
  //   (xy)'
endmodule

module Full_Adder (
  input  c,
  input  x,
  input  y,
  output out_4,
  output c___1
);

  wire half_adder_1_acarreo, half_adder_1_x_y__xy__prime, half_adder_2_acarreo;

  Half_Adder half_adder_1 (.x(x), .y(y), .x_y__xy__prime(half_adder_1_x_y__xy__prime), .Acarreo(half_adder_1_acarreo));
  Half_Adder half_adder_2 (
    .x(c), .y(half_adder_1_x_y__xy__prime), .x_y__xy__prime(out_4), .Acarreo(half_adder_2_acarreo));
  or or_1 (c___1, half_adder_2_acarreo, half_adder_1_acarreo);

  // Notes on the sheet:
  //   FULL-ADDER
  //   suma xy
  //   acarreo xy
  //   suma bits s
  //   acarreo = c
endmodule

module Circuito_Final (
  input  x1,
  input  y1,
  input  x2,
  input  y2,
  input  x3,
  input  y3,
  output out_7,
  output out_8,
  output out_9,
  output out_10
);

  wire full_adder_1_c___1, half_adder_1_acarreo;

  Half_Adder half_adder_1 (.x(x1), .y(y1), .x_y__xy__prime(out_7), .Acarreo(half_adder_1_acarreo));
  Full_Adder full_adder_1 (.c(half_adder_1_acarreo), .x(x2), .y(y2), .out_4(out_8), .c___1(full_adder_1_c___1));
  Full_Adder full_adder_2 (.c(full_adder_1_c___1), .x(x3), .y(y3), .out_4(out_9), .c___1(out_10));

  // Notes on the sheet:
  //   x
  //   y
  //   half-adder
  //   suma x1 + y1
  //   acarreo x1 + y1
  //   c1
  //   SUMADOR DE DOS NÚMEROS DE 3 BITS
  //   full-adder
  //   suma x2 + y2
  //   acarreo x2 + y2
  //   c2
  //   full-adder
  //   suma x3 + y3
  //   acarreo x3 + y3
  //   c3
endmodule
