// Logisim project Ejercicio2.circ as structural Verilog: 1 circuit, main circuit main
module main (
  input  M,
  input  F1,
  input  F2,
  input  F3,
  output out_5
);

  wire and_1_out, and_2_out, and_3_out, not_1_out, not_2_out, not_3_out, not_4_out;

  not not_1 (not_1_out, M);
  not not_2 (not_2_out, F1);
  not not_3 (not_3_out, F2);
  not not_4 (not_4_out, F3);
  and and_1 (and_1_out, not_1_out, F1, not_3_out, not_4_out);
  and and_2 (and_2_out, not_1_out, not_2_out, F2, not_4_out);
  and and_3 (and_3_out, not_1_out, not_2_out, not_3_out, F3);
  or or_1 (out_5, and_1_out, and_2_out, and_3_out);

  // Notes on the sheet:
  //   CIRCUITO DE UN ELEVADOR
endmodule
