// Logisim project Ejercicio3.circ as structural Verilog: 1 circuit, main circuit main
module main (
  input  x,
  input  y,
  input  z,
  input  x_2,
  input  y_2,
  input  z_2,
  output out_7,
  output out_8
);

  wire and_1_out, and_2_out, and_3_out, and_4_out, and_5_out, and_6_out, not_1_out, not_2_out, not_3_out,
       not_4_out;

  not not_1 (not_1_out, x);
  not not_2 (not_2_out, y);
  not not_3 (not_3_out, z);
  not not_4 (not_4_out, y_2);
  and and_1 (and_1_out, x_2, y_2);
  and and_2 (and_2_out, not_4_out, z_2);
  and and_3 (and_3_out, x, y, z);
  and and_4 (and_4_out, x, y, not_3_out);
  and and_5 (and_5_out, x, not_2_out, z);
  and and_6 (and_6_out, not_1_out, not_2_out, z);
  or or_1 (out_8, and_1_out, and_2_out);
  or or_2 (out_7, and_3_out, and_4_out, and_5_out, and_6_out);

  // Notes on the sheet:
  //   CIRCUITO NORMAL
  //   CIRCUITO MINIMIZADO
endmodule
