// Logisim project Ejercicio4.circ as structural Verilog: 1 circuit, main circuit main
module main (
  input  J,
  input  L,
  input  K,
  output out_4
);

  wire and_1_out, and_2_out, not_1_out, not_2_out;

  not not_1 (not_1_out, J);
  not not_2 (not_2_out, L);
  and and_1 (and_1_out, J, L, K);
  and and_2 (and_2_out, not_1_out, not_2_out, K);
  or or_1 (out_4, and_1_out, and_2_out);

  // Notes on the sheet:
  //   CIRCUITO PARA UNA CAJA FUERTE
endmodule
